# Fritzing sketch Automacao (saved by Fritzing 0.9.3b)
breadboards: 1

parts:
  Componente1 = Arduino Uno (Rev3)
  LED1 = LED - 5mm [color="Red (633nm)" package="5 mm [THT]"]
  LED2 = LED - 5mm [color="Red (633nm)" package="5 mm [THT]"]
  R2 = Resistor [tolerance=±5% resistance=330 package=THT]
  R3 = Resistor [tolerance=±5% resistance=220 package=THT]

nets:
  N1: Componente1.D12/MISO, LED2.anode
  N2: Componente1.D13/SCK, LED1.anode
  N3: Componente1.GND, R2.Pin_0, R3.Pin_0
  N4: LED1.cathode, R3.Pin_1
  N5: LED2.cathode, R2.Pin_1
