# Fritzing sketch HC_SR04 (saved by Fritzing 0.9.3b)
breadboards: 1

parts:
  Componente1 = Arduino Uno (Rev3)
  hc-sr1 = hc-sr04
  LED1 = LED - 5mm [color="Red (633nm)" package="5 mm [THT]"]
  R1 = Resistor [tolerance=±5% resistance=220 package=THT]

nets:
  N1: Componente1.D12/MISO, hc-sr1.Trig
  N2: Componente1.D13/SCK, hc-sr1.Echo
  N3: Componente1.D2, LED1.anode
  5V: Componente1.5V, hc-sr1.VCC
  GND: Componente1.GND, hc-sr1.GND, R1.Pin_0
  N4: LED1.cathode, R1.Pin_1
