# Fritzing sketch Leitura_Analogica_LDR (saved by Fritzing 0.9.3b)
circuit board: 8.46667cm x 5.64444cm
breadboards: 1

parts:
  Componente1 = Arduino Uno (Rev3)
  R1 = Photocell (LDR) [package=THT]
  R2 = Resistor [tolerance=±5% resistance=10k package=THT]
  LED1 = LED - 5mm [color="White (4500K)" package="5 mm [THT]"]
  R3 = Resistor [tolerance=±5% resistance=100 package=THT]

nets:
  N1: Componente1.A0, R1.pin_0, R2.Pin_1
  N2: Componente1.GND, R2.Pin_0, R3.Pin_0
  N3: Componente1.D2, LED1.anode
  N4: Componente1.5V, R1.pin_1
  N5: LED1.cathode, R3.Pin_1
