# Fritzing sketch superMaquina (saved by Fritzing 0.9.3b)
circuit board: 6.94388cm x 5.54826cm
breadboards: 1

parts:
  LED1 = LED - 5mm [color="Red (633nm)" package="5 mm [THT]"]
  R1 = Resistor [tolerance=±5% resistance=330 package=THT]
  Componente1 = Arduino Uno (Rev3)
  LED4 = LED - 5mm [color="Red (633nm)" package="5 mm [THT]"]
  LED5 = LED - 5mm [color="Red (633nm)" package="5 mm [THT]"]
  LED6 = LED - 5mm [color="Red (633nm)" package="5 mm [THT]"]
  LED7 = LED - 5mm [color="Red (633nm)" package="5 mm [THT]"]
  LED8 = LED - 5mm [color="Red (633nm)" package="5 mm [THT]"]
  R2 = Resistor [tolerance=±5% resistance=330 package=THT]
  R3 = Resistor [tolerance=±5% resistance=330 package=THT]
  R4 = Resistor [tolerance=±5% resistance=330 package=THT]
  R5 = Resistor [tolerance=±5% resistance=330 package=THT]
  R6 = Resistor [tolerance=±5% resistance=330 package=THT]

nets:
  N1: LED1.cathode, R1.Pin_0
  N2: LED1.anode, Componente1.D13/SCK
  N3: R1.Pin_1, Componente1.GND, R2.Pin_1, R3.Pin_1, R4.Pin_1, R5.Pin_1, R6.Pin_1
  N4: Componente1.D8, LED4.anode
  N5: Componente1.D9_PWM, LED6.anode
  N6: Componente1.D10_PWM/SS, LED5.anode
  N7: Componente1.D11_PWM/MOSI, LED8.anode
  N8: Componente1.D12/MISO, LED7.anode
  N9: LED4.cathode, R6.Pin_0
  N10: LED5.cathode, R5.Pin_0
  N11: LED6.cathode, R4.Pin_0
  N12: LED7.cathode, R3.Pin_0
  N13: LED8.cathode, R2.Pin_0

// code stored in the sketch: superMaquina.ino
/**
 * Sequencial de LEDs  (efeito Supermáquina)
 * @Author Eugenio Ramos Junior 
 */
 

 void setup() {
  pinMode(13, OUTPUT);
}

void loop() {
  digitalWrite(13, HIGH); 
}
